# Fritzing sketch Diagrama conexiones - Wifi Car (saved by Fritzing 0.9.3b)

parts:
  Part1 = Adafruit FeatherWing Doubler [part_number="Adafruit #2890"]
  Part2 = Adafruit Feather HUZZAH ESP8266 [part_number="Adafruit #2821"]  # not connected
  Part3 = Adafruit DC+Stepper FeatherWing [part_number="Adafruit #2927"]
  M1 = DC Motor
  M2 = DC Motor
  BAT1 = BC9VPC [package=bc9vpc]

nets:
  N1: Part1.O, Part3.N
  N2: Part1.M, Part3.L
  N3: Part1.I, Part3.H
  N4: Part1.RX, Part3.RX
  N5: Part1.F, Part3.F
  GND: Part1.GND, Part3.GND, BAT1.V-
  N6: Part1.G, Part3.G
  N7: Part1.TX, Part3.TX
  N8: Part1.MOSI, Part3.MOSI
  N9: Part1.A, Part3.A
  N10: Part1.VBAT, Part3.VBAT
  N11: Part1.EN, Part3.EN
  N12: Part1.USB, Part3.USB
  N13: Part1.L, Part3.K
  N14: Part1.SCL, Part3.SCL
  N15: Part1.3V, Part3.+3.3V
  N16: Part1.AREF, Part3.AREF
  N17: Part1.B, Part3.B
  N18: Part1.C, Part3.C
  N19: Part1.D, Part3.D
  N20: Part1.E, Part3.E
  N21: Part1.SCK, Part3.SCK
  N22: Part1.SDA, Part3.SDA
  N23: Part1.J, Part3.I
  N24: Part1.K, Part3.J
  N25: Part1.N, Part3.M
  N26: Part1.RESET, Part3.RESET
  N27: Part1.MISO, Part3.MISO
  N28: Part3.VMOTOR, BAT1.V+
  N29: Part3.M3B, M2.pin_1
  N30: Part3.M3A, M2.pin_2
  N31: Part3.M4A, M1.pin_1
  N32: Part3.M4B, M1.pin_2

custom parts:
  Adafruit FeatherWing Doubler: This is the FeatherWing Doubler - a prototyping add-on and more for all Feather boards. This is similar to our FeatherWing Proto except there are two! The magic of the Doubler comes when stacking a Feather and another board on top of the Doubler so you can work with both boards simultaneously side-by-side! The Doubler, like the Proto, has a duplicate breakout for each pin on a Feather, as well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
  Adafruit Feather HUZZAH ESP8266: his is the Adafruit Feather HUZZAH ESP8266 - our take on an 'all-in-one' ESP8266 WiFi development board with built in USB and battery charging. Its an ESP8266 WiFi module with all the extras you need, ready to rock! We have other boards in the Feather family, check'em out here. At the Feather HUZZAH's heart is an ESP8266 WiFi microcontroller clocked at 80 MHz and at 3.3V logic. This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
  Adafruit DC+Stepper FeatherWing: This is the DC Motor + Stepper FeatherWing which will let you use 2 x bi-polar stepper motors or 4 x brushed DC motorx (or 1 stepper and 2 DC motors). Using our Feather Stacking Headers or Feather Female Headers you can connect a FeatherWing on top or bottom of your Feather board and let the board take flight! The original Adafruit Motorshield Kit is one of our most beloved kits, which is why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
